# Fritzing sketch Fritzing Motor Routing (saved by Fritzing 0.9.2b)
breadboards: 1

parts:
  Part1 = Arduino Uno (Rev3)
  J1 = Basic Servo

nets:
  N1: Part1.D9_PWM, J1.pulse
  5V: Part1.5V, J1.vcc
  GND: Part1.GND, J1.gnd

// code stored in the sketch: Motor Code.ino
/*
 Controlling a servo position using a potentiometer (variable resistor)
 by Michal Rinott <http://people.interaction-ivrea.it/m.rinott>

 modified on 8 Nov 2013
 by Scott Fitzgerald
 http://www.arduino.cc/en/Tutorial/Knob
*/

#include <Servo.h>

Servo myservo;  // create servo object to control a servo


void setup() {
  myservo.attach(9);  // attaches the servo on pin 9 to the servo object
}

void loop() {
 
  myservo.write(90);                  // sets the servo position according to the scaled value
  delay(1000);                           // waits for the servo to get there
  myservo.write(1);                  // sets the servo position according to the scaled value
  delay(1000);                           // waits for the servo to get there
}
